// Logisim project labo3.circ as structural Verilog: 8 circuits, main circuit main
module main (
);


  // Notes on the sheet:
  //   Attention, votre version de Logisim
  //   ne contient pas de tracker. Si vous
  //   enregistrez votre projet, toutes les
  //   informations du tracker seront
  //   définitivement effacées.
endmodule

module CUSTOM (
  input  [3:0] A,
  input  [3:0] B,
  input  in_3
);

  wire add1bit_1_c_out, add1bit_2_c_out, add1bit_3_c_out;
  wire [3:0] add1bit_1_d;

  ADD1BIT add1bit_1 (.A(A[0]), .B(A[1]), .D(add1bit_1_d[0]), .C_out(add1bit_1_c_out));  // open: C_in
  ADD1BIT add1bit_2 (.A(A[2]), .B(A[3]), .C_in(add1bit_1_c_out), .D(add1bit_1_d[1]), .C_out(add1bit_2_c_out));
  ADD1BIT add1bit_3 (.A(B[0]), .B(B[1]), .C_in(add1bit_2_c_out), .D(add1bit_1_d[2]), .C_out(add1bit_3_c_out));
  ADD1BIT add1bit_4 (.A(B[2]), .B(B[3]), .C_in(add1bit_3_c_out), .D(add1bit_1_d[3]));  // open: C_out

  // Notes on the sheet:
  //   Attention, votre version de Logisim
  //   ne contient pas de tracker. Si vous
  //   enregistrez votre projet, toutes les
  //   informations du tracker seront
  //   définitivement effacées.
endmodule

module ADD1BIT (
  input  A,
  input  B,
  input  C_in,
  output D,
  output C_out
);

  wire and_1_out, and_2_out, and_3_out, xor_1_out;

  xor xor_1 (xor_1_out, A, B);
  and and_1 (and_1_out, A, B);
  and and_2 (and_2_out, A, C_in);
  and and_3 (and_3_out, B, C_in);
  or or_1 (C_out, and_1_out, and_2_out, and_3_out);
  xor xor_2 (D, xor_1_out, C_in);

  // Notes on the sheet:
  //   Attention, votre version de Logisim
  //   ne contient pas de tracker. Si vous
  //   enregistrez votre projet, toutes les
  //   informations du tracker seront
  //   définitivement effacées.
endmodule

module ADDSUB_ALU (
  input  Sub,
  input  [3:0] A,
  input  [3:0] B,
  output [3:0] R,
  output R3,
  output ZERO
);

  ADD_SUB4BITS add_sub4bits_1 (.Sub(Sub), .A(A), .B(B), .D(R));  // open: C_out
  BitSelector #(.width(4)) bitselector_1 (.in(R), .out(R3), .sel(2'b11));
  ISZERO_4BITS iszero_4bits_1 (.A(R), .D(ZERO));

  // Notes on the sheet:
  //   Attention, votre version de Logisim
  //   ne contient pas de tracker. Si vous
  //   enregistrez votre projet, toutes les
  //   informations du tracker seront
  //   définitivement effacées.
endmodule

module ADD_SUB4BITS (
  input  Sub,
  input  [3:0] A,
  input  [3:0] B,
  output [3:0] D,
  output C_out
);

  wire [3:0] comp2_4bits_1_d;

  COMP2_4BITS comp2_4bits_1 (.S(Sub), .A(B), .D(comp2_4bits_1_d));
  ADD4BITS add4bits_1 (.A(A), .B(comp2_4bits_1_d), .D(D), .C_out(C_out));  // open: C_in

  // Notes on the sheet:
  //   Attention, votre version de Logisim
  //   ne contient pas de tracker. Si vous
  //   enregistrez votre projet, toutes les
  //   informations du tracker seront
  //   définitivement effacées.
endmodule

module ADD4BITS (
  input  [3:0] A,
  input  [3:0] B,
  input  C_in,
  output [3:0] D,
  output C_out
);

  wire add1bit_1_c_out, add1bit_2_c_out, add1bit_3_c_out;

  ADD1BIT add1bit_1 (.A(A[0]), .B(B[0]), .C_in(C_in), .D(D[0]), .C_out(add1bit_1_c_out));
  ADD1BIT add1bit_2 (.A(A[1]), .B(B[1]), .C_in(add1bit_1_c_out), .D(D[1]), .C_out(add1bit_2_c_out));
  ADD1BIT add1bit_3 (.A(A[2]), .B(B[2]), .C_in(add1bit_2_c_out), .D(D[2]), .C_out(add1bit_3_c_out));
  ADD1BIT add1bit_4 (.A(A[3]), .B(B[3]), .C_in(add1bit_3_c_out), .D(D[3]), .C_out(C_out));

  // Notes on the sheet:
  //   Attention, votre version de Logisim
  //   ne contient pas de tracker. Si vous
  //   enregistrez votre projet, toutes les
  //   informations du tracker seront
  //   définitivement effacées.
endmodule

module COMP2_4BITS (
  input  S,
  input  [3:0] A,
  output [3:0] D
);

  wire [3:0] xor_1_out;

  xor xor_1 (xor_1_out[0], S, A[0]);
  xor xor_2 (xor_1_out[1], S, A[1]);
  xor xor_3 (xor_1_out[2], S, A[2]);
  xor xor_4 (xor_1_out[3], S, A[3]);
  ADD4BITS add4bits_1 (.A(xor_1_out), .C_in(S), .D(D));  // open: B, C_out

  // Notes on the sheet:
  //   Attention, votre version de Logisim
  //   ne contient pas de tracker. Si vous
  //   enregistrez votre projet, toutes les
  //   informations du tracker seront
  //   définitivement effacées.
endmodule

module ISZERO_4BITS (
  input  [3:0] A,
  output D
);

  wire or_1_out, or_2_out;

  or or_1 (or_1_out, A[0], A[1]);
  or or_2 (or_2_out, A[2], A[3]);
  nor nor_1 (D, or_1_out, or_2_out);

  // Notes on the sheet:
  //   Attention, votre version de Logisim
  //   ne contient pas de tracker. Si vous
  //   enregistrez votre projet, toutes les
  //   informations du tracker seront
  //   définitivement effacées.
endmodule
